// Logisim project memory.circ as structural Verilog: 1 circuit, main circuit main
module main (
  output [15:0] out_1,
  output [31:0] out_2,
  output [31:0] t0,
  output [31:0] t1,
  output [31:0] a0,
  output [31:0] inst,
  output halt
);

  wire clk;
  wire [15:0] adder_1_out;
  wire [23:0] bit_extender_1_out;
  wire [31:0] ra, s0, s1, shifter_1_out, sp;

  Comparator #(.width(16), .mode("unsigned")) comparator_1 (.a(16'hc), .b(out_1), .eq(halt));  // open: gt, lt
  CPU cpu_1 (.CLK(clk), .Instruction(inst), .PC(out_2), .s0(s0), .s1(s1), .t0(t0), .t1(t1), .a0(a0), .ra(ra), .sp(sp));
  Clock clock_1 (.out(clk));
  Register #(.width(16)) register_1 (.D(adder_1_out), .Q(out_1), .clk(clk));  // open: en, clr
  Adder #(.width(16)) adder_1 (.a(16'h1), .b(out_1), .out(adder_1_out));  // open: cin, cout
  Shifter #(.width(32), .shift("lr")) shifter_1 (.in(out_2), .\dist (5'b00010), .out(shifter_1_out));
  Bit_Extender #(.in_width(32), .out_width(24)) bit_extender_1 (.in(shifter_1_out), .out(bit_extender_1_out));
  ROM #(.addrWidth(24), .dataWidth(32)) rom_1 (.addr(bit_extender_1_out), .data(inst), .sel(1'b1));

  // Other names for the same wires on the sheet: fetch_addr[31:0] = out_2; In[15:0] = out_1; instruction[31:0] = inst

  // Notes on the sheet:
  //   Halt signal
  //   Counter
  //   These are debug/test outputs from your circuit
  //   contents of rom_1 (hex, n*v repeats v):
  //   12345437 67840413 2802423 2802283 ff00513 a02223 400283 401283 10537 fff50513 a02623 c01283
endmodule
